# Fritzing sketch Lab 1 and 2 Connections (saved by Fritzing 0.9.3b)
breadboards: 1

parts:
  VCC1 = 4 x AAA Battery Mount
  U1 = L298_BRIDGE_DRIVER [package=powerso20]
  Raspberry_Pi_1 = Raspberry Pi 3 [part_number=RPI-3-V1.2]
  M1 = DC Motor
  M2 = DC Motor

nets:
  N1: VCC1.-, U1.GND
  N2: VCC1.+, U1.VS
  N3: U1.OUT1, M1.pin_2
  N4: U1.OUT2, M1.pin_1
  N5: U1.IN1, Raspberry_Pi_1.GPIO20
  N6: U1.ENA, Raspberry_Pi_1.GPIO21
  N7: U1.IN2, Raspberry_Pi_1.GPIO16
  VSS: U1.VSS, Raspberry_Pi_1.5V
  N8: U1.IN3, Raspberry_Pi_1.GPIO12
  N9: U1.ENB, Raspberry_Pi_1.GPIO8
  N10: U1.IN4, Raspberry_Pi_1.GPIO7
  N11: U1.OUT3, M2.pin_2
  N12: U1.OUT4, M2.pin_1

notes:
  Lab 1 and 2 Wiring Diagram
  IN4 to GPIO7
  ENB TO GPIO8
  IN3 TO GPIO12
  IN2 To GPIO16
  IN1 TO GPIO20
  ENA To GPIO21
  5V Logic Power
  Right Motor
  Left Motor
  POWER CELL (6V)
