# Fritzing sketch Lab 3 Connections (saved by Fritzing 0.9.3b)
breadboards: 1

parts:
  Raspberry_Pi_2 = Raspberry Pi 3 [part_number=RPI-3-V1.2]
  U2 = L298_BRIDGE_DRIVER [package=powerso20]
  VCC2 = 4 x AAA Battery Mount
  M3 = DC Motor
  M4 = DC Motor
  LineFollow_Right = KY-033 Tracing Black White Line Hunting Sensor Module For Arduino
  LineFollow_Center = KY-033 Tracing Black White Line Hunting Sensor Module For Arduino
  LineFollow_Left = KY-033 Tracing Black White Line Hunting Sensor Module For Arduino

nets:
  N1: Raspberry_Pi_2.GPIO13, LineFollow_Left.S
  N2: Raspberry_Pi_2.GPIO19, LineFollow_Center.S
  N3: Raspberry_Pi_2.GPIO26, LineFollow_Right.S
  N4: Raspberry_Pi_2.GPIO21, U2.ENA
  N5: Raspberry_Pi_2.GPIO20, U2.IN1
  N6: Raspberry_Pi_2.GPIO16, U2.IN2
  N7: Raspberry_Pi_2.GPIO12, U2.IN3
  N8: Raspberry_Pi_2.GPIO7, U2.IN4
  N9: Raspberry_Pi_2.GPIO8, U2.ENB
  GND: Raspberry_Pi_2.GND, LineFollow_Right.GND, LineFollow_Center.GND, LineFollow_Left.GND
  5V: Raspberry_Pi_2.5V, U2.VSS, LineFollow_Right.V+, LineFollow_Center.V+, LineFollow_Left.V+
  N10: U2.GND, VCC2.-
  N11: U2.OUT1, M4.pin_2
  N12: U2.OUT2, M4.pin_1
  N13: U2.VS, VCC2.+
  N14: U2.OUT3, M3.pin_2
  N15: U2.OUT4, M3.pin_1

notes:
  IN4 to GPIO7
  ENB TO GPIO8
  IN3 TO GPIO12
  IN2 TO GPIO16
  IN1 TO GPIO20
  ENA TO GPIO21
  5V Logic Power
  Right Motor
  Left Motor
  POWER CELL (6V)
  Lab 3 Wiring Diagram
  Raspberry Pi 3B
  Left Sensor
  Center Sensor
  Right Sensor

custom parts:
  KY-033 Tracing Black White Line Hunting Sensor Module For Arduino: Tracing Black White Line Hunting Sensor Module For Arduino Description: This is KY-033 tracking sensor. The KY-033 measures the intensity of infrared radiation and delivers it as an analog output voltage. Features: Operating voltage: 2.5 - 12V(cannot over12V) working current: 18mA-20mA at 5V Enhanced accuracy Documents: http://www.vishay.com/docs/83760/tcrt5000.pdf
